// Logisim project 0611q1.circ as structural Verilog: 1 circuit, main circuit main
module main (
  input  shift_right,
  input  I4,
  input  I3,
  input  I2,
  input  shift_left,
  input  I1,
  input  in_7,
  input  in_8,
  input  in_9,
  input  in_10,
  output Q4,
  output Q3,
  output Q2,
  output Q1
);

  wire clock_1_out, multiplexer_1_out, multiplexer_2_out, multiplexer_3_out, multiplexer_4_out;

  Multiplexer #(.select(2)) multiplexer_1 (
    .in0(Q4), .in1(shift_right), .in2(Q3), .in3(I4), .out(multiplexer_1_out), .sel({in_10, in_9}));
  Multiplexer #(.select(2)) multiplexer_2 (
    .in0(Q3), .in1(Q4), .in2(Q2), .in3(I3), .out(multiplexer_2_out), .sel({in_10, in_9}));
  Multiplexer #(.select(2)) multiplexer_3 (
    .in0(Q2), .in1(Q3), .in2(Q1), .in3(I2), .out(multiplexer_3_out), .sel({in_10, in_9}));
  Multiplexer #(.select(2)) multiplexer_4 (
    .in0(Q1), .in1(Q2), .in2(shift_left), .in3(I1), .out(multiplexer_4_out), .sel({in_10, in_9}));
  D_Flip_Flop d_ff_1 (.D(multiplexer_1_out), .clk(clock_1_out), .Q(Q4), .preset(in_8), .reset(in_7));  // open: Qn
  D_Flip_Flop d_ff_2 (.D(multiplexer_2_out), .clk(clock_1_out), .Q(Q3), .preset(in_8), .reset(in_7));  // open: Qn
  D_Flip_Flop d_ff_3 (.D(multiplexer_3_out), .clk(clock_1_out), .Q(Q2), .preset(in_8), .reset(in_7));  // open: Qn
  D_Flip_Flop d_ff_4 (.D(multiplexer_4_out), .clk(clock_1_out), .Q(Q1), .preset(in_8), .reset(in_7));  // open: Qn
  Clock clock_1 (.out(clock_1_out));

  // Notes on the sheet:
  //   S0
  //   S1
  //   R
  //   S
endmodule
