// Logisim project 1410q1.circ as structural Verilog: 1 circuit, main circuit main
module main (
  input  A3,
  input  B3,
  input  A2,
  input  B2,
  input  A1,
  input  B1,
  input  A0,
  input  B0,
  input  C0,
  output C,
  output S3,
  output S2,
  output S1,
  output SO
);

  wire C1_out, C2_out, C3_out, G0_out, G1_out, G2_out, G3_out, P0_out, P0C0_out, P1_out, P1G0_out,
       P1P0C0_out, P2_out, P2G1_out, P2P1G0_out, P2P1P0C0_out, P3_out, P3G2_out, P3P2G1_out, P3P2P1G0_out,
       P3P2P1P0C0_out;

  and G3 (G3_out, A3, B3);
  and G2 (G2_out, A2, B2);
  and G1 (G1_out, A1, B1);
  and G0 (G0_out, A0, B0);
  xor P3 (P3_out, A3, B3);
  xor P2 (P2_out, A2, B2);
  xor P1 (P1_out, A1, B1);
  xor P0 (P0_out, A0, B0);
  and P0C0 (P0C0_out, P0_out, C0);
  and P3G2 (P3G2_out, G2_out, P3_out);
  and P3P2G1 (P3P2G1_out, P3_out, P2_out, G1_out);
  and P3P2P1G0 (P3P2P1G0_out, P3_out, P2P1G0_out);
  and P3P2P1P0C0 (P3P2P1P0C0_out, P3_out, P2P1P0C0_out);
  and P2P1P0C0 (P2P1P0C0_out, P2_out, C0, P0_out, P1_out);
  and P2G1 (P2G1_out, G1_out, P2_out);
  and P2P1G0 (P2P1G0_out, P2_out, G0_out, P1_out);
  and P1G0 (P1G0_out, P1_out, G0_out);
  and P1P0C0 (P1P0C0_out, P1_out, P0_out, C0);
  or C4 (C, G3_out, P3G2_out, P3P2G1_out, P3P2P1G0_out, P3P2P1P0C0_out);
  or C3 (C3_out, G2_out, P2P1P0C0_out, P2G1_out, P2P1G0_out);
  or C2 (C2_out, G1_out, P1G0_out, P1P0C0_out);
  or C1 (C1_out, G0_out, P0C0_out);
  xor xor_1 (S3, P3_out, C3_out);
  xor xor_2 (S2, P2_out, C2_out);
  xor xor_3 (S1, C1_out, P1_out);
  xor xor_4 (SO, P0_out, C0);
endmodule
