// Logisim project 1410q2.circ as structural Verilog: 7 circuits, main circuit main
module main (
  input  A3,
  input  B3,
  input  A2,
  input  B2,
  input  A1,
  input  B1,
  input  A0,
  input  B0,
  output Aisgreater,
  output Aissmaller,
  output Aisequal
);

  wire ornor_1_s;

  Agreater agreater_1 (.A3(A3), .B3(B3), .A2(A2), .B2(B2), .A1(A1), .B1(B1), .A0(A0), .B0(B0), .Agre(Aisgreater));
  Aequal aequal_1 (.A3(A3), .B3(B3), .A2(A2), .B2(B2), .A1(A1), .B1(B1), .A0(A0), .B0(B0), .aequ(Aisequal));
  ornor ornor_1 (.A(Aisgreater), .B(Aisequal), .S(ornor_1_s));
  notnor notnor_1 (.A(ornor_1_s), .A1(Aissmaller));
endmodule

module andnor (
  input  A,
  input  B,
  output S
);

  wire nor_1_out, nor_2_out;

  nor nor_1 (nor_1_out, A, A);
  nor nor_2 (nor_2_out, B, B);
  nor nor_3 (S, nor_1_out, nor_2_out);
endmodule

module ornor (
  input  A,
  input  B,
  output S
);

  wire nor_1_out;

  nor nor_1 (nor_1_out, A, B);
  nor nor_2 (S, nor_1_out, nor_1_out);
endmodule

module xornor (
  input  A,
  input  B,
  output AxorB
);

  wire andnor_1_s, andnor_2_s, notnor_1_a1, notnor_2_a1;

  notnor notnor_1 (.A(A), .A1(notnor_1_a1));
  notnor notnor_2 (.A(B), .A1(notnor_2_a1));
  andnor andnor_1 (.A(A), .B(notnor_2_a1), .S(andnor_1_s));
  andnor andnor_2 (.A(notnor_1_a1), .B(B), .S(andnor_2_s));
  ornor ornor_1 (.A(andnor_1_s), .B(andnor_2_s), .S(AxorB));
endmodule

module notnor (
  input  A,
  output A1
);

  nor nor_1 (A1, A, A);
endmodule

module Agreater (
  input  A3,
  input  B3,
  input  A2,
  input  B2,
  input  A1,
  input  B1,
  input  A0,
  input  B0,
  output Agre
);

  wire andnor_1_s, andnor_2_s, andnor_3_s, andnor_4_s, andnor_5_s, andnor_6_s, andnor_7_s, andnor_8_s,
       andnor_9_s, notnor_1_a1, notnor_2_a1, notnor_3_a1, notnor_4_a1, notnor_5_a1, notnor_6_a1, notnor_7_a1,
       ornor_1_s, ornor_2_s, xornor_1_axorb, xornor_2_axorb, xornor_3_axorb;

  notnor notnor_1 (.A(B3), .A1(notnor_1_a1));
  notnor notnor_2 (.A(B2), .A1(notnor_2_a1));
  notnor notnor_3 (.A(B1), .A1(notnor_3_a1));
  notnor notnor_4 (.A(B0), .A1(notnor_4_a1));
  andnor andnor_1 (.A(A3), .B(notnor_1_a1), .S(andnor_1_s));
  xornor xornor_1 (.A(B3), .B(A3), .AxorB(xornor_1_axorb));
  andnor andnor_2 (.A(A2), .B(notnor_2_a1), .S(andnor_2_s));
  xornor xornor_2 (.A(B2), .B(A2), .AxorB(xornor_2_axorb));
  andnor andnor_3 (.A(A1), .B(notnor_3_a1), .S(andnor_3_s));
  xornor xornor_3 (.A(B1), .B(A1), .AxorB(xornor_3_axorb));
  andnor andnor_4 (.A(A0), .B(notnor_4_a1), .S(andnor_4_s));
  notnor notnor_5 (.A(xornor_2_axorb), .A1(notnor_5_a1));
  notnor notnor_6 (.A(xornor_3_axorb), .A1(notnor_6_a1));
  notnor notnor_7 (.A(xornor_1_axorb), .A1(notnor_7_a1));
  andnor andnor_5 (.A(notnor_7_a1), .B(notnor_5_a1), .S(andnor_5_s));
  andnor andnor_6 (.A(andnor_5_s), .B(notnor_6_a1), .S(andnor_6_s));
  andnor andnor_7 (.A(notnor_7_a1), .B(andnor_2_s), .S(andnor_7_s));
  andnor andnor_8 (.A(andnor_5_s), .B(andnor_3_s), .S(andnor_8_s));
  andnor andnor_9 (.A(andnor_6_s), .B(andnor_4_s), .S(andnor_9_s));
  ornor ornor_1 (.A(andnor_1_s), .B(andnor_7_s), .S(ornor_1_s));
  ornor ornor_2 (.A(andnor_8_s), .B(andnor_9_s), .S(ornor_2_s));
  ornor ornor_3 (.A(ornor_1_s), .B(ornor_2_s), .S(Agre));
endmodule

module Aequal (
  input  A3,
  input  B3,
  input  A2,
  input  B2,
  input  A1,
  input  B1,
  input  A0,
  input  B0,
  output aequ
);

  wire andnor_1_s, andnor_2_s, notnor_1_a1, notnor_2_a1, notnor_3_a1, notnor_4_a1, xornor_1_axorb,
       xornor_2_axorb, xornor_3_axorb, xornor_4_axorb;

  xornor xornor_1 (.A(A3), .B(B3), .AxorB(xornor_1_axorb));
  xornor xornor_2 (.A(A2), .B(B2), .AxorB(xornor_2_axorb));
  xornor xornor_3 (.A(A1), .B(B1), .AxorB(xornor_3_axorb));
  xornor xornor_4 (.A(A0), .B(B0), .AxorB(xornor_4_axorb));
  notnor notnor_1 (.A(xornor_1_axorb), .A1(notnor_1_a1));
  notnor notnor_2 (.A(xornor_2_axorb), .A1(notnor_2_a1));
  notnor notnor_3 (.A(xornor_3_axorb), .A1(notnor_3_a1));
  notnor notnor_4 (.A(xornor_4_axorb), .A1(notnor_4_a1));
  andnor andnor_1 (.A(notnor_1_a1), .B(notnor_2_a1), .S(andnor_1_s));
  andnor andnor_2 (.A(notnor_3_a1), .B(notnor_4_a1), .S(andnor_2_s));
  andnor andnor_3 (.A(andnor_1_s), .B(andnor_2_s), .S(aequ));
endmodule
